# Fritzing sketch rebound_build07 (saved by Fritzing 0.9.1b)
breadboards: 2

parts:
  Part1 = Arduino Uno (Rev3)
  U1 = 74HC595 [package="DIP16 [THT]"]
  R1 = Resistor [tolerance=±5% resistance=270 package=THT]
  R2 = Resistor [tolerance=±5% resistance=270 package=THT]
  R3 = Resistor [tolerance=±5% resistance=270 package=THT]
  LED0 = LED - 5mm [color="Red (633nm)" package="5 mm [THT]"]
  RGB_home_LED = RGB LED - (4 legs) [package="5 mm [THT]"]
  S1 = Pushbutton [package="[THT]"]
  LED1 = LED - 5mm [color="Red (633nm)" package="5 mm [THT]"]
  LED2 = LED - 5mm [color="Red (633nm)" package="5 mm [THT]"]
  LED3 = LED - 5mm [color="Red (633nm)" package="5 mm [THT]"]
  LED4 = LED - 5mm [color="Red (633nm)" package="5 mm [THT]"]
  LED5 = LED - 5mm [color="Red (633nm)" package="5 mm [THT]"]
  LED6 = LED - 5mm [color="Red (633nm)" package="5 mm [THT]"]
  LED7 = LED - 5mm [color="Red (633nm)" package="5 mm [THT]"]
  R4 = Resistor [tolerance=±5% resistance=470 package=THT]
  R5 = Resistor [tolerance=±5% resistance=470 package=THT]
  R6 = Resistor [tolerance=±5% resistance=470 package=THT]
  R7 = Resistor [tolerance=±5% resistance=470 package=THT]
  R8 = Resistor [tolerance=±5% resistance=470 package=THT]
  R9 = Resistor [tolerance=±5% resistance=470 package=THT]
  R10 = Resistor [tolerance=±5% resistance=470 package=THT]
  R11 = Resistor [tolerance=±5% resistance=470 package=THT]

nets:
  N1: Part1.D8, U1.DS
  N2: Part1.D9_PWM, U1.ST_CP
  N3: Part1.D10_PWM/SS, U1.SH_CP
  N4: Part1.D12/MISO, U1.MR
  N5: Part1.D13/SCK, S1.Pin_1, S1.Pin_2
  N6: Part1.D3_PWM, R1.Pin_1
  N7: Part1.D5_PWM, R2.Pin_1
  N8: Part1.D6_PWM, R3.Pin_1
  5V: Part1.5V, U1.VCC, RGB_home_LED.common_anode
  GND: Part1.GND, U1.GND, U1.OE
  N9: U1.Q1, LED1.anode
  N10: U1.Q2, LED2.anode
  N11: U1.Q3, LED3.anode
  N12: U1.Q4, LED4.anode
  N13: U1.Q5, LED5.anode
  N14: U1.Q6, LED6.anode
  N15: U1.Q7, LED7.anode
  N16: U1.Q0, LED0.anode
  N17: R1.Pin_0, RGB_home_LED.red_cathode
  N18: R2.Pin_0, RGB_home_LED.green_cathode
  N19: R3.Pin_0, RGB_home_LED.blue_cathode
  N20: LED0.cathode, R4.Pin_1
  N21: S1.Pin_3, S1.Pin_4, R4.Pin_0, R5.Pin_0, R6.Pin_0, R7.Pin_0, R8.Pin_0, R9.Pin_0, R10.Pin_0, R11.Pin_0
  N22: LED1.cathode, R5.Pin_1
  N23: LED2.cathode, R6.Pin_1
  N24: LED3.cathode, R7.Pin_1
  N25: LED4.cathode, R8.Pin_1
  N26: LED5.cathode, R9.Pin_1
  N27: LED6.cathode, R10.Pin_1
  N28: LED7.cathode, R11.Pin_1
