# Fritzing sketch rebound_build08 (saved by Fritzing 0.9.1b)
breadboards: 2

parts:
  Part1 = Arduino Uno (Rev3)
  U1 = 74HC595 [package="DIP16 [THT]"]
  R1 = Resistor [tolerance=±5% resistance=270 package=THT]
  R2 = Resistor [tolerance=±5% resistance=270 package=THT]
  R3 = Resistor [tolerance=±5% resistance=270 package=THT]
  LED0 = LED - 5mm [color="Red (633nm)" package="5 mm [THT]"]
  RGB_home_LED = RGB LED - (4 legs) [package="5 mm [THT]"]
  S1 = Pushbutton [package="[THT]"]
  LED1 = LED - 5mm [color="Red (633nm)" package="5 mm [THT]"]
  LED2 = LED - 5mm [color="Red (633nm)" package="5 mm [THT]"]
  LED3 = LED - 5mm [color="Red (633nm)" package="5 mm [THT]"]
  LED4 = LED - 5mm [color="Red (633nm)" package="5 mm [THT]"]
  LED5 = LED - 5mm [color="Red (633nm)" package="5 mm [THT]"]
  LED6 = LED - 5mm [color="Red (633nm)" package="5 mm [THT]"]
  LED7 = LED - 5mm [color="Red (633nm)" package="5 mm [THT]"]
  R4 = Resistor [tolerance=±5% resistance=470 package=THT]
  R5 = Resistor [tolerance=±5% resistance=470 package=THT]
  R6 = Resistor [tolerance=±5% resistance=470 package=THT]
  R7 = Resistor [tolerance=±5% resistance=470 package=THT]
  R8 = Resistor [tolerance=±5% resistance=470 package=THT]
  R9 = Resistor [tolerance=±5% resistance=470 package=THT]
  R10 = Resistor [tolerance=±5% resistance=470 package=THT]
  R11 = Resistor [tolerance=±5% resistance=470 package=THT]
  RGB_home_LED1 = RGB LED - (4 legs) [package="5 mm [THT]"]
  S2 = Pushbutton [package="[THT]"]
  R12 = Resistor [tolerance=±5% resistance=270 package=THT]
  R13 = Resistor [tolerance=±5% resistance=270 package=THT]
  R14 = Resistor [tolerance=±5% resistance=270 package=THT]

nets:
  N1: Part1.D8, U1.DS
  N2: Part1.D9_PWM, R1.Pin_1
  N3: Part1.D10_PWM/SS, R2.Pin_1
  N4: Part1.D11_PWM/MOSI, R3.Pin_1
  N5: Part1.D12/MISO, U1.MR
  N6: Part1.D13/SCK, S1.Pin_1, S1.Pin_2
  N7: Part1.D2, S2.Pin_1, S2.Pin_2
  N8: Part1.D3_PWM, R12.Pin_1
  N9: Part1.D4, U1.ST_CP
  N10: Part1.D5_PWM, R13.Pin_1
  N11: Part1.D6_PWM, R14.Pin_1
  N12: Part1.D7, U1.SH_CP
  5V: Part1.5V, U1.VCC, RGB_home_LED.common_anode, RGB_home_LED1.common_anode
  GND: Part1.GND, U1.GND, U1.OE
  N13: U1.Q1, LED1.anode
  N14: U1.Q2, LED2.anode
  N15: U1.Q3, LED3.anode
  N16: U1.Q4, LED4.anode
  N17: U1.Q5, LED5.anode
  N18: U1.Q6, LED6.anode
  N19: U1.Q7, LED7.anode
  N20: U1.Q0, LED0.anode
  N21: R1.Pin_0, RGB_home_LED.red_cathode
  N22: R2.Pin_0, RGB_home_LED.green_cathode
  N23: R3.Pin_0, RGB_home_LED.blue_cathode
  N24: LED0.cathode, R4.Pin_1
  N25: S1.Pin_3, S1.Pin_4, R4.Pin_0, R5.Pin_0, R6.Pin_0, R7.Pin_0, R8.Pin_0, R9.Pin_0, R10.Pin_0, R11.Pin_0, S2.Pin_3, S2.Pin_4
  N26: LED1.cathode, R5.Pin_1
  N27: LED2.cathode, R6.Pin_1
  N28: LED3.cathode, R7.Pin_1
  N29: LED4.cathode, R8.Pin_1
  N30: LED5.cathode, R9.Pin_1
  N31: LED6.cathode, R10.Pin_1
  N32: LED7.cathode, R11.Pin_1
  N33: RGB_home_LED1.red_cathode, R12.Pin_0
  N34: RGB_home_LED1.green_cathode, R13.Pin_0
  N35: RGB_home_LED1.blue_cathode, R14.Pin_0
